# Fritzing sketch Schéma électrique (saved by Fritzing 0.9.3b)
breadboards: 1

parts:
  Composant1 = NRF24L01+ Breakout Board  # not connected
  Composant2 = NRF24L01+ Breakout Board  # not connected
  Composant3 = Arduino Mega 2560 (Rev3)
  M1 = DC Motor  # not connected
  M2 = DC Motor  # not connected
  J1 = Basic Servo  # not connected
  L1 = Solenoid
  L2 = Solenoid
  L3 = Solenoid
  L4 = Solenoid
  M3 = DC Motor  # not connected
  M4 = DC Motor  # not connected
  U2 = LIPO-2000mAh [package=lipo-2000]
  Q1 = NPN-Transistor [package="SOT-23 [SMD]"]
  Q2 = NPN-Transistor [package="SOT-23 [SMD]"]
  Q3 = NPN-Transistor [package="SOT-23 [SMD]"]

nets:
  N1: Composant3.GND, Q1.1, Q2.1, Q3.1
  N2: Composant3.D5_PWM, Q3.0
  N3: Composant3.D6_PWM, Q2.0
  N4: Composant3.D7_PWM, Q1.0
  N5: L1.pin1, L2.pin1, Q1.2
  N6: L1.pin2, L2.pin2, L3.pin2, L4.pin2, U2.+
  N7: L3.pin1, Q3.2
  N8: L4.pin1, Q2.2

notes:
  Vérins
  Vérin Mât
  Vérin mat de grande vergue
  Vérin de la croix X2

// code stored in the sketch: Untitled2.ino
void setup()
{
  pinMode(7, OUTPUT);
}

void loop()
{
  analogWrite(7, 0);
  delay(1000); // Wait for 1000 millisecond(s)
  analogWrite(7,127);
  delay(1000);
  analogWrite(7, 255);
  delay(1000); // Wait for 1000 millisecond(s)
}
